// Logisim project MCU_CC3Mc_24_1(MarcosVinicius).circ as structural Verilog: 15 circuits, main circuit main
module main (
  input  in_1,
  output Ov,
  output Zero
);

  wire alu_1_overflow, alu_1_zero, clock_1_out, clock_2_out, clock_3_out, not_1_out;
  wire [3:0] ac_1_q, alu_1_s, counter_1_q, mux_1_s, ram_1_data;
  wire [7:0] ir_1_q, rom_1_data;

  Clock clock_1 (.out(clock_1_out));
  Counter #(.width(4), .max('hf)) counter_1 (.Q(counter_1_q), .clk(clock_1_out));  // open: load, D, count, carry, clr
  ROM #(.addrWidth(4)) rom_1 (.addr(counter_1_q), .data(rom_1_data));  // open: sel
  IR ir_1 (.in_2(rom_1_data), .CLOCK(clock_1_out), .Q(ir_1_q));
  // Probe on ac_1_q
  Clock clock_2 (.out(clock_2_out));
  Clock clock_3 (.out(clock_3_out));
  Mux mux_1 (.E(ir_1_q[3:0]), .Controle(ir_1_q[4]), .D(ram_1_data), .S(mux_1_s));
  // Probe on mux_1_s
  ALU alu_1 (
    .D(ir_1_q[4]), .A(ac_1_q), .B(mux_1_s), .\Operações (ir_1_q[7:5]), .s(alu_1_s),
    .Overflow(alu_1_overflow), .Zero(alu_1_zero));
  // Probe on alu_1_s
  AC ac_1 (.D(alu_1_s), .CLOCK(clock_2_out), .Q(ac_1_q));
  D_Flip_Flop d_ff_1 (.clk(clock_2_out), .D(alu_1_overflow), .Q(Ov));  // open: Qn, preset, en, reset
  D_Flip_Flop d_ff_2 (.clk(clock_2_out), .D(alu_1_zero), .Q(Zero));  // open: Qn, preset, en, reset
  RAM #(.addrWidth(4), .dataWidth(4)) ram_1 (
    .addr(ir_1_q[3:0]), .data(ram_1_data), .clk(clock_3_out), .ld(in_1));  // open: sel, clr
  not not_1 (not_1_out, in_1);
  BUFFER buffer_1 (.B(ac_1_q), .in_2(not_1_out), .S(ram_1_data));

  // Notes on the sheet:
  //   Overflow
  //   Overflow
endmodule

module ADD_1 (
  input  A,
  input  B,
  input  Vem_1,
  output S,
  output Vai_1
);

  wire and_1_out, and_2_out, or_1_out, xor_1_out;

  or or_1 (or_1_out, B, Vem_1);
  and and_1 (and_1_out, B, Vem_1);
  xor xor_1 (xor_1_out, A, B);
  and and_2 (and_2_out, or_1_out, A);
  xor xor_2 (S, xor_1_out, Vem_1);
  or or_2 (Vai_1, and_2_out, and_1_out);
endmodule

module ADD_4 (
  input  [3:0] B,
  input  [3:0] A,
  input  in_3,
  output out_4,
  output [3:0] out_5
);

  wire add_1_2_vai_1, add_1_3_vai_1, add_1_4_vai_1;

  ADD_1 add_1_1 (.A(A[3]), .B(B[3]), .Vem_1(add_1_2_vai_1), .S(out_5[3]), .Vai_1(out_4));
  ADD_1 add_1_2 (.A(A[2]), .B(B[2]), .Vem_1(add_1_4_vai_1), .S(out_5[2]), .Vai_1(add_1_2_vai_1));
  ADD_1 add_1_3 (.A(A[0]), .B(B[0]), .Vem_1(in_3), .S(out_5[0]), .Vai_1(add_1_3_vai_1));
  ADD_1 add_1_4 (.A(A[1]), .B(B[1]), .Vem_1(add_1_3_vai_1), .S(out_5[1]), .Vai_1(add_1_4_vai_1));
endmodule

module SUB_1 (
  input  A,
  input  B,
  input  Vem_1,
  output S,
  output Vai_1
);

  wire and_1_out, and_2_out, or_1_out, xor_1_out;

  or or_1 (or_1_out, B, Vem_1);
  and and_1 (and_1_out, B, Vem_1);
  xor xor_1 (xor_1_out, A, B);
  and and_2 (and_2_out, or_1_out, ~A);  // AND_Gate
  xor xor_2 (S, xor_1_out, Vem_1);
  or or_2 (Vai_1, and_2_out, and_1_out);
endmodule

module SUB_4 (
  input  [3:0] B,
  input  [3:0] A,
  input  in_3,
  output out_4,
  output [3:0] S
);

  wire sub_1_2_vai_1, sub_1_3_vai_1, sub_1_4_vai_1;

  SUB_1 sub_1_1 (.A(A[3]), .B(B[3]), .Vem_1(sub_1_2_vai_1), .S(S[3]), .Vai_1(out_4));
  SUB_1 sub_1_2 (.A(A[2]), .B(B[2]), .Vem_1(sub_1_3_vai_1), .S(S[2]), .Vai_1(sub_1_2_vai_1));
  SUB_1 sub_1_3 (.A(A[1]), .B(B[1]), .Vem_1(sub_1_4_vai_1), .S(S[1]), .Vai_1(sub_1_3_vai_1));
  SUB_1 sub_1_4 (.A(A[0]), .B(B[0]), .Vem_1(in_3), .S(S[0]), .Vai_1(sub_1_4_vai_1));
endmodule

module BUFFER (
  input  [3:0] B,
  input  in_2,
  output [3:0] S
);

  assign S[2] = in_2 ? B[2] : 1'bz;  // Controlled_Buffer controlled_buffer_1
  assign S[3] = in_2 ? B[3] : 1'bz;  // Controlled_Buffer controlled_buffer_2
  assign S[0] = in_2 ? B[0] : 1'bz;  // Controlled_Buffer controlled_buffer_3
  assign S[1] = in_2 ? B[1] : 1'bz;  // Controlled_Buffer controlled_buffer_4
endmodule

module BUFFER_NEGATIVE (
  input  [3:0] B,
  input  in_2,
  output [3:0] S
);

  assign S[3] = in_2 ? ~B[3] : 1'bz;  // Controlled_Inverter controlled_inverter_1
  assign S[2] = in_2 ? ~B[2] : 1'bz;  // Controlled_Inverter controlled_inverter_2
  assign S[1] = in_2 ? ~B[1] : 1'bz;  // Controlled_Inverter controlled_inverter_3
  assign S[0] = in_2 ? ~B[0] : 1'bz;  // Controlled_Inverter controlled_inverter_4
endmodule

module DEC_3X8 (
  input  [2:0] \Operação ,
  output S0,
  output S1,
  output S2,
  output S3,
  output S4,
  output S5,
  output S6,
  output S7
);

  wire not_1_out, not_2_out, not_3_out, not_4_out, not_5_out, not_6_out, not_7_out, not_8_out, not_9_out,
       not_10_out, not_11_out, not_12_out;

  not not_1 (not_1_out, \Operação [2]);
  not not_2 (not_2_out, \Operação [1]);
  not not_3 (not_3_out, \Operação [0]);
  not not_4 (not_4_out, \Operação [2]);
  not not_5 (not_5_out, \Operação [1]);
  not not_6 (not_6_out, \Operação [2]);
  not not_7 (not_7_out, \Operação [0]);
  not not_8 (not_8_out, \Operação [2]);
  not not_9 (not_9_out, \Operação [1]);
  not not_10 (not_10_out, \Operação [0]);
  not not_11 (not_11_out, \Operação [1]);
  not not_12 (not_12_out, \Operação [0]);
  and and_1 (S0, not_1_out, not_2_out, not_3_out);
  and and_2 (S1, not_4_out, not_5_out, \Operação [0]);
  and and_3 (S2, not_6_out, \Operação [1], not_7_out);
  and and_4 (S3, not_8_out, \Operação [1], \Operação [0]);
  and and_5 (S4, \Operação [2], not_9_out, not_10_out);
  and and_6 (S5, \Operação [2], not_11_out, \Operação [0]);
  and and_7 (S6, \Operação [2], \Operação [1], not_12_out);
  and and_8 (S7, \Operação [2], \Operação [1], \Operação [0]);
endmodule

module ROT_L (
  input  [1:0] XY,
  input  [3:0] ABCD,
  output [3:0] abcd_2
);

  wire and_1_out, and_2_out, and_3_out, and_4_out, and_5_out, and_6_out, and_7_out, and_8_out, and_9_out;

  and and_1 (and_1_out, ~XY[1], ~XY[0], ABCD[3]);  // AND_Gate
  and and_2 (and_2_out, ~XY[1], XY[0], ABCD[2]);  // AND_Gate
  and and_3 (and_3_out, XY[1], ~XY[0], ABCD[1]);  // AND_Gate
  and and_4 (and_4_out, XY[1], XY[0], ABCD[0]);
  and and_5 (and_5_out, ~XY[1], ~XY[0], ABCD[2]);  // AND_Gate
  and and_6 (and_6_out, ~XY[1], XY[0], ABCD[1]);  // AND_Gate
  and and_7 (and_7_out, XY[1], ~XY[0], ABCD[0]);  // AND_Gate
  and and_8 (and_8_out, ~XY[1], ~XY[0], ABCD[1]);  // AND_Gate
  and and_9 (and_9_out, ~XY[1], XY[0], ABCD[0]);  // AND_Gate
  and and_10 (abcd_2[3], ~XY[1], ~XY[0], ABCD[0]);  // AND_Gate
  or or_1 (abcd_2[0], and_1_out, and_2_out, and_3_out, and_4_out);
  or or_2 (abcd_2[1], and_5_out, and_6_out, and_7_out);
  or or_3 (abcd_2[2], and_8_out, and_9_out);
endmodule

module ROT_W (
  input  [1:0] XY,
  input  [3:0] ABCD,
  output [3:0] abcd_2
);

  wire and_1_out, and_2_out, and_3_out, and_4_out, and_5_out, and_6_out, and_7_out, and_8_out, and_9_out;

  and and_1 (and_1_out, ~XY[1], ~XY[0], ABCD[0]);  // AND_Gate
  and and_2 (and_2_out, ~XY[1], XY[0], ABCD[1]);  // AND_Gate
  and and_3 (and_3_out, XY[1], ~XY[0], ABCD[2]);  // AND_Gate
  and and_4 (and_4_out, XY[1], XY[0], ABCD[3]);
  and and_5 (and_5_out, ~XY[1], ~XY[0], ABCD[1]);  // AND_Gate
  and and_6 (and_6_out, ~XY[1], XY[0], ABCD[2]);  // AND_Gate
  and and_7 (and_7_out, XY[1], ~XY[0], ABCD[3]);  // AND_Gate
  and and_8 (and_8_out, ~XY[1], ~XY[0], ABCD[2]);  // AND_Gate
  and and_9 (and_9_out, ~XY[1], XY[0], ABCD[3]);  // AND_Gate
  and and_10 (abcd_2[3], ~XY[1], ~XY[0], ABCD[3]);  // AND_Gate
  or or_1 (abcd_2[0], and_1_out, and_2_out, and_3_out, and_4_out);
  or or_2 (abcd_2[1], and_5_out, and_6_out, and_7_out);
  or or_3 (abcd_2[2], and_8_out, and_9_out);
endmodule

module OR_4 (
  input  [3:0] B,
  input  [3:0] A,
  output [3:0] S
);

  or or_1 (S[2], A[2], B[2]);
  or or_2 (S[3], A[3], B[3]);
  or or_3 (S[1], A[1], B[1]);
  or or_4 (S[0], A[0], B[0]);
endmodule

module ALU (
  input  D,
  input  [3:0] A,
  input  [3:0] B,
  input  [2:0] \Operações ,
  output Overflow,
  output [3:0] s,
  output Zero
);

  wire add_4_1_out_4, and_1_out, and_2_out, dec_3x8_1_s0, dec_3x8_1_s1, dec_3x8_1_s2, dec_3x8_1_s3,
       dec_3x8_1_s4, dec_3x8_1_s5, dec_3x8_1_s6, dec_3x8_1_s7, not_1_out, sub_4_1_out_4;
  wire [3:0] add_4_1_out_5, buffer_5_s, or_4_1_s, rot_l_1_abcd_2, rot_w_1_abcd_2, sub_4_1_s;

  or or_1 (Overflow, and_1_out, and_2_out);
  and and_1 (and_1_out, add_4_1_out_4, dec_3x8_1_s1);
  and and_2 (and_2_out, sub_4_1_out_4, dec_3x8_1_s2);
  DEC_3X8 dec_3x8_1 (
    .\Operação (\Operações ), .S0(dec_3x8_1_s0), .S1(dec_3x8_1_s1), .S2(dec_3x8_1_s2), .S3(dec_3x8_1_s3),
    .S4(dec_3x8_1_s4), .S5(dec_3x8_1_s5), .S6(dec_3x8_1_s6), .S7(dec_3x8_1_s7));
  BUFFER buffer_1 (.B(B), .in_2(dec_3x8_1_s0), .S(s));
  nor nor_1 (Zero, dec_3x8_1_s7, dec_3x8_1_s6, s[0], s[1], s[2], s[3]);
  ADD_4 add_4_1 (.A(A), .out_4(add_4_1_out_4), .B(B), .in_3(1'b0), .out_5(add_4_1_out_5));
  BUFFER buffer_2 (.B(add_4_1_out_5), .in_2(dec_3x8_1_s1), .S(s));
  SUB_4 sub_4_1 (.A(A), .out_4(sub_4_1_out_4), .B(B), .in_3(1'b0), .S(sub_4_1_s));
  BUFFER buffer_3 (.B(sub_4_1_s), .in_2(dec_3x8_1_s2), .S(s));
  OR_4 or_4_1 (.A(A), .B(B), .S(or_4_1_s));
  BUFFER buffer_4 (.B(or_4_1_s), .in_2(dec_3x8_1_s3), .S(s));
  BUFFER_NEGATIVE buffer_negative_1 (.B(B), .in_2(dec_3x8_1_s4), .S(s));
  not not_1 (not_1_out, D);
  ROT_W rot_w_1 (.XY(B[1:0]), .abcd_2(rot_w_1_abcd_2), .ABCD(A));
  ROT_L rot_l_1 (.XY(B[1:0]), .abcd_2(rot_l_1_abcd_2), .ABCD(A));
  BUFFER buffer_5 (.B(rot_w_1_abcd_2), .in_2(D), .S(buffer_5_s));
  BUFFER buffer_6 (.B(rot_l_1_abcd_2), .in_2(not_1_out), .S(buffer_5_s));
  BUFFER buffer_7 (.B(buffer_5_s), .in_2(dec_3x8_1_s5), .S(s));
endmodule

module AC (
  input  CLOCK,
  input  [3:0] D,
  output [3:0] Q
);

  D_Flip_Flop d_ff_1 (.clk(CLOCK), .D(D[3]), .Q(Q[3]));  // open: Qn, preset, en, reset
  D_Flip_Flop d_ff_2 (.clk(CLOCK), .D(D[2]), .Q(Q[2]));  // open: Qn, preset, en, reset
  D_Flip_Flop d_ff_3 (.clk(CLOCK), .D(D[1]), .Q(Q[1]));  // open: Qn, preset, en, reset
  D_Flip_Flop d_ff_4 (.clk(CLOCK), .D(D[0]), .Q(Q[0]));  // open: Qn, preset, en, reset

  // Notes on the sheet:
  //   D3
  //   D2
  //   D1
  //   D0
endmodule

module Mux (
  input  [3:0] E,
  input  [3:0] D,
  input  Controle,
  output [3:0] S
);

  wire not_1_out;

  not not_1 (not_1_out, Controle);
  BUFFER buffer_1 (.B(E), .in_2(not_1_out), .S(S));
  BUFFER buffer_2 (.B(D), .in_2(Controle), .S(S));
endmodule

module IR (
  input  CLOCK,
  input  [7:0] in_2,
  output [7:0] Q
);

  D_Flip_Flop d_ff_1 (.clk(CLOCK), .D(in_2[7]), .Q(Q[7]));  // open: Qn, preset, en, reset
  D_Flip_Flop d_ff_2 (.clk(CLOCK), .D(in_2[6]), .Q(Q[6]));  // open: Qn, preset, en, reset
  D_Flip_Flop d_ff_3 (.clk(CLOCK), .D(in_2[5]), .Q(Q[5]));  // open: Qn, preset, en, reset
  D_Flip_Flop d_ff_4 (.clk(CLOCK), .D(in_2[4]), .Q(Q[4]));  // open: Qn, preset, en, reset
  D_Flip_Flop d_ff_5 (.clk(CLOCK), .D(in_2[3]), .Q(Q[3]));  // open: Qn, preset, en, reset
  D_Flip_Flop d_ff_6 (.clk(CLOCK), .D(in_2[2]), .Q(Q[2]));  // open: Qn, preset, en, reset
  D_Flip_Flop d_ff_7 (.clk(CLOCK), .D(in_2[1]), .Q(Q[1]));  // open: Qn, preset, en, reset
  D_Flip_Flop d_ff_8 (.clk(CLOCK), .D(in_2[0]), .Q(Q[0]));  // open: Qn, preset, en, reset

  // Notes on the sheet:
  //   D3
  //   D2
  //   D1
  //   D0
  //   D2
  //   D3
  //   D
  //   D1
  //   D0
endmodule
